# Fritzing sketch ground-station-circuit (saved by Fritzing 0.9.3b)
breadboards: 2

parts:
  M1 = DOIT Esp32 DevKit v1 (30 pins long, 11 pins width) [part_number=ESP32S-PIN30]
  ENCODER1 = Rotary Encoder with Knob
  Part1 = Adafruit RFM9x LoRa Radio [part_number="Adafruit #3072 and #3073"]
  Part2 = OLED Monochrome 128x64 1.3 inch [part_number=938]
  R1 = Rotary Potentiometer (Small) [maximum_resistance=100kΩ package=THT]
  R2 = Rotary Potentiometer (Small) [maximum_resistance=100kΩ package=THT]
  LED1 = LED - 5mm [color="Red (633nm)" package="5 mm [THT]"]
  LED2 = LED - 5mm [color="Blue (430nm)" package="5 mm [THT]"]
  S1 = Pushbutton [package="[THT]"]
  S2 = Pushbutton [package="[THT]"]
  S3 = Toggle Switch [package=THT]
  VCC1 = Battery block 9V

nets:
  VIN: M1.3V3, ENCODER1.no_name_yet#4, Part1.VIN, Part2.VIN, R1.leg1, R2.leg2
  GND: M1.GND, ENCODER1.no_name_yet#2, Part1.GND, Part2.GND, R1.leg2, R2.leg1, LED1.cathode, LED2.cathode, S1.Pin_4, S2.Pin_1, S2.Pin_2, VCC1.-
  N1: M1.D2, Part1.DIO0
  N2: M1.D4, Part1.CS
  N3: M1.RX2, Part1.RST
  N4: M1.D5, S1.Pin_2
  N5: M1.D18, Part1.SCK
  N6: M1.D19, Part1.MISO
  N7: M1.D21, Part2.MOSI_SDA
  N8: M1.D22, Part2.SCLK_SCK
  N9: M1.D23, Part1.MOSI
  N10: M1.D34, S2.Pin_4
  N11: M1.D35, ENCODER1.no_name_yet#1
  N12: M1.D32, ENCODER1.no_name_yet#5
  N13: M1.D33, ENCODER1.no_name_yet#3
  N14: M1.D25, R1.wiper
  N15: M1.D26, R2.wiper
  N16: M1.D27, Part2.RESET
  N17: M1.D12, LED2.anode
  N18: M1.D13, LED1.anode
  N19: M1.VIN, S3.COM
  N20: S3.L1, VCC1.+

notes:
  + sw
  clk gnd dt

custom parts:
  DOIT Esp32 DevKit v1 (30 pins long, 11 pins width): The DOIT Esp32 DevKit v1 is one of the development board created by DOIT to evaluate the ESP-WROOM-32 module. It is based on the ESP32 microcontroller that boasts Wifi, Bluetooth, Ethernet and Low Power support all in a single chip. (vanepp) made breadboard work, adjusted pin numbering and labels and reduced size of schematic and cleaned up pcb. This chip is 30pins long (2 x15) and 11 pins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
  Rotary Encoder with Knob: Rotary Encoder with 1/4" Shaft and Knob
  Adafruit RFM9x LoRa Radio: Sending data over long distances is like magic, and now you can be a magician with this range of powerful and easy-to-use radio modules. Sure, sometimes you want to talk to a computer (a good time to use WiFi) or perhaps communicate with a Phone (choose Bluetooth Low Energy!) but what if you want to send data very far? Most WiFi, Bluetooth, Zigbee and other wireless chipsets use 2.4GHz, which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
  OLED Monochrome 128x64 1.3 inch: These displays are small, only about 1.3" diagonal, but very readable due to the high contrast of an OLED display. This display is made of 128x64 individual white OLED pixels, each one is turned on or off by the controller chip. Because the display makes its own light, no backlight is required. This reduces the power required to run the OLED and is why the display has such high contrast; we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
